// Logisim project square_root.circ as structural Verilog
module main (
  input  [7:0] Entrada_X,
  output [7:0] Display
);

  wire CLK_out, clock_1_out, clock_2_out, comparator_1_gt, comparator_1_lt;
  wire [7:0] adder_2_out, adder_3_out, adder_4_out, multiplexer_1_out, Reg_D_q, Reg_R_q, Reg_S_q;

  Register Reg_R (.D(Display), .Q(Reg_R_q), .clk(CLK_out));  // open: en, clr
  Clock CLK (.out(CLK_out));
  Adder adder_1 (.a(Reg_R_q), .b(8'h1), .out(Display));  // open: cin, cout
  Clock clock_1 (.out(clock_1_out));
  Clock clock_2 (.out(clock_2_out));
  Register Reg_D (.D(adder_2_out), .Q(Reg_D_q), .clk(CLK_out));  // open: en, clr
  Adder adder_2 (.a(Reg_D_q), .b(8'h2), .out(adder_2_out));  // open: cin, cout
  Comparator_part comparator_1 (
    .a(Entrada_X), .b(adder_4_out), .gt(comparator_1_gt), .lt(comparator_1_lt));  // open: eq
  Register Reg_S (.D(adder_4_out), .Q(Reg_S_q), .clk(CLK_out));  // open: en, clr
  Adder adder_3 (.a(adder_2_out), .b(8'h1), .out(adder_3_out));  // open: cin, cout
  Multiplexer #(.width(8)) multiplexer_1 (
    .in0(8'h4), .in1(adder_3_out), .out(multiplexer_1_out), .sel(clock_1_out), .en(clock_2_out));
  Adder adder_4 (.a(Reg_S_q), .b(multiplexer_1_out), .out(adder_4_out));  // open: cin, cout

  // Notes on the sheet:
  //   CONTROLE
  //   r+1
  //   enquanto t = 1
  //   01 = 4
  //   11 = (d+1)
  //   d+2
  //   s > x
  //   d+1
  //   4 ou (d+1)
  //   s+d+1
endmodule
